// Logisim project M2 Circuitos Digitais - Karin Araldi e Ana Beatriz da Conceição.circ as structural Verilog: 16 circuits, main circuit Ula
module main (
  input  [3:0] A,
  input  [3:0] B,
  input  [2:0] in_3,
  output out_4,
  output out_5,
  output [3:0] out_6
);

  wire displays_1_a, displays_1_b, displays_1_c, displays_1_d, displays_1_e, displays_1_f, displays_1_g,
       displays_1_h, displays_2_a, displays_2_b, displays_2_c, displays_2_d, displays_2_e, displays_2_f,
       displays_2_g, displays_2_h, displays_3_a, displays_3_b, displays_3_c, displays_3_d, displays_3_e,
       displays_3_f, displays_3_g, displays_3_h;

  Displays displays_1 (
    .in_1(A[3]), .in_2(A[2]), .in_3(A[1]), .in_4(A[0]), .A(displays_1_a), .B(displays_1_b), .C(displays_1_c),
    .D(displays_1_d), .E(displays_1_e), .F(displays_1_f), .G(displays_1_g), .H(displays_1_h));
  _7_Segment_Display u_7_segment_display_1 (
    .g(displays_1_g), .f(displays_1_f), .a(displays_1_a), .b(displays_1_b), .e(displays_1_e),
    .d(displays_1_d), .c(displays_1_c), .dp(displays_1_h));
  Ula ula_1 (.out_4(out_6), .A(A), .B(B), .OF(out_5), .ZF(out_4), .in_3(in_3));
  Displays displays_2 (
    .in_1(B[3]), .in_2(B[2]), .in_3(B[1]), .in_4(B[0]), .A(displays_2_a), .B(displays_2_b), .C(displays_2_c),
    .D(displays_2_d), .E(displays_2_e), .F(displays_2_f), .G(displays_2_g), .H(displays_2_h));
  Displays displays_3 (
    .in_1(out_6[3]), .in_2(out_6[2]), .in_3(out_6[1]), .in_4(out_6[0]), .A(displays_3_a), .B(displays_3_b),
    .C(displays_3_c), .D(displays_3_d), .E(displays_3_e), .F(displays_3_f), .G(displays_3_g), .H(displays_3_h));
  _7_Segment_Display u_7_segment_display_2 (
    .g(displays_2_g), .f(displays_2_f), .a(displays_2_a), .b(displays_2_b), .e(displays_2_e),
    .d(displays_2_d), .c(displays_2_c), .dp(displays_2_h));
  _7_Segment_Display u_7_segment_display_3 (
    .g(displays_3_g), .f(displays_3_f), .a(displays_3_a), .b(displays_3_b), .e(displays_3_e),
    .d(displays_3_d), .c(displays_3_c), .dp(displays_3_h));
endmodule

module Ula (
  input  [3:0] A,
  input  [3:0] B,
  input  [2:0] in_3,
  output [3:0] out_4,
  output OF,
  output ZF
);

  wire \Adição_out_4 , Decremento_out_4, displays_1_a, displays_1_b, displays_1_c, displays_1_d,
       displays_1_e, displays_1_f, displays_1_g, displays_1_h, displays_2_a, displays_2_b, displays_2_c,
       displays_2_d, displays_2_e, displays_2_f, displays_2_g, displays_2_h, displays_3_a, displays_3_b,
       displays_3_c, displays_3_d, displays_3_e, displays_3_f, displays_3_g, displays_3_h, Incremento_out_4,
       not_2_out, not_3_out, not_4_out, not_5_out, \Subtração_out_4 ;
  wire [3:0] \Adição_out_5 , and_1_out_3, Decremento_out_5, Incremento_out_5, not_1_out_2, Or_out_3,
       \Subtração_out_5 ;

  Displays displays_1 (
    .in_1(A[3]), .in_2(A[2]), .in_3(A[1]), .in_4(A[0]), .A(displays_1_a), .B(displays_1_b), .C(displays_1_c),
    .D(displays_1_d), .E(displays_1_e), .F(displays_1_f), .G(displays_1_g), .H(displays_1_h));
  _7_Segment_Display u_7_segment_display_1 (
    .g(displays_1_g), .f(displays_1_f), .a(displays_1_a), .b(displays_1_b), .e(displays_1_e),
    .d(displays_1_d), .c(displays_1_c), .dp(displays_1_h));
  Displays displays_2 (
    .in_1(B[3]), .in_2(B[2]), .in_3(B[1]), .in_4(B[0]), .A(displays_2_a), .B(displays_2_b), .C(displays_2_c),
    .D(displays_2_d), .E(displays_2_e), .F(displays_2_f), .G(displays_2_g), .H(displays_2_h));
  _7_Segment_Display u_7_segment_display_2 (
    .g(displays_2_g), .f(displays_2_f), .a(displays_2_a), .b(displays_2_b), .e(displays_2_e),
    .d(displays_2_d), .c(displays_2_c), .dp(displays_2_h));
  SomaESub Decremento (.A(A), .B(4'b0001), .Seletor(1'b1), .out_5(Decremento_out_5), .out_4(Decremento_out_4));
  SomaESub Incremento (.A(A), .B(4'b0001), .Seletor(1'b0), .out_5(Incremento_out_5), .out_4(Incremento_out_4));
  SomaESub \Adição  (.A(A), .B(B), .Seletor(1'b0), .out_5(\Adição_out_5 ), .out_4(\Adição_out_4 ));
  SomaESub \Subtração  (.A(A), .B(B), .Seletor(1'b1), .out_5(\Subtração_out_5 ), .out_4(\Subtração_out_4 ));
  Not not_1 (.in_1(A), .out_2(not_1_out_2));
  Ou Or (.A(A), .B(B), .out_3(Or_out_3));
  And and_1 (.A(A), .B(B), .out_3(and_1_out_3));
  Multiplexer #(.select(3), .width(4), .enable("false")) multiplexer_1 (
    .in0(A), .in1(Decremento_out_5), .in2(Incremento_out_5), .in3(\Adição_out_5 ), .in4(\Subtração_out_5 ),
    .in5(not_1_out_2), .in6(Or_out_3), .in7(and_1_out_3), .out(out_4), .sel(in_3));
  Displays displays_3 (
    .in_1(out_4[3]), .in_2(out_4[2]), .in_3(out_4[1]), .in_4(out_4[0]), .A(displays_3_a), .B(displays_3_b),
    .C(displays_3_c), .D(displays_3_d), .E(displays_3_e), .F(displays_3_f), .G(displays_3_g), .H(displays_3_h));
  Multiplexer #(.select(3), .enable("false")) multiplexer_2 (
    .in0(1'b0), .in1(Decremento_out_4), .in2(Incremento_out_4), .in3(\Adição_out_4 ),
    .in4(\Subtração_out_4 ), .in5(1'b0), .in6(1'b0), .in7(1'b0), .out(OF), .sel(in_3));
  _7_Segment_Display u_7_segment_display_3 (
    .g(displays_3_g), .f(displays_3_f), .a(displays_3_a), .b(displays_3_b), .e(displays_3_e),
    .d(displays_3_d), .c(displays_3_c), .dp(displays_3_h));
  not not_2 (not_2_out, out_4[3]);
  not not_3 (not_3_out, out_4[1]);
  not not_4 (not_4_out, out_4[2]);
  not not_5 (not_5_out, out_4[0]);
  and and_2 (ZF, not_2_out, not_4_out, not_3_out, not_5_out);

  // Notes on the sheet:
  //   Pass
  //   Not
  //   And
endmodule

module somador (
  input  A,
  input  B,
  input  Cin,
  output S,
  output Carry
);

  wire and_1_out, and_2_out, and_3_out, xor_1_out;

  xor xor_1 (xor_1_out, A, B);
  xor xor_2 (S, xor_1_out, Cin);
  and and_1 (and_1_out, A, B);
  and and_2 (and_2_out, A, Cin);
  and and_3 (and_3_out, B, Cin);
  or or_1 (Carry, and_1_out, and_2_out, and_3_out);
endmodule

module SomaESub (
  input  [3:0] A,
  input  [3:0] B,
  input  Seletor,
  output out_4,
  output [3:0] out_5
);

  wire somador_2_carry, somador_3_carry, somador_4_carry, xor_1_out, xor_2_out, xor_3_out, xor_4_out;

  xor xor_1 (xor_1_out, Seletor, B[3]);
  somador somador_1 (.A(A[3]), .B(xor_1_out), .S(out_5[3]), .Carry(out_4), .Cin(somador_2_carry));
  xor xor_2 (xor_2_out, Seletor, B[2]);
  somador somador_2 (.A(A[2]), .B(xor_2_out), .S(out_5[2]), .Carry(somador_2_carry), .Cin(somador_3_carry));
  xor xor_3 (xor_3_out, Seletor, B[1]);
  somador somador_3 (.A(A[1]), .B(xor_3_out), .S(out_5[1]), .Carry(somador_3_carry), .Cin(somador_4_carry));
  xor xor_4 (xor_4_out, Seletor, B[0]);
  somador somador_4 (.A(A[0]), .B(xor_4_out), .S(out_5[0]), .Carry(somador_4_carry), .Cin(Seletor));

  // Notes on the sheet:
  //   0 = soma
  //   1 = subtração
endmodule

module Ou (
  input  [3:0] A,
  input  [3:0] B,
  output [3:0] out_3
);

  or or_1 (out_3[0], A[0], B[0]);
  or or_2 (out_3[1], A[1], B[1]);
  or or_3 (out_3[2], A[2], B[2]);
  or or_4 (out_3[3], A[3], B[3]);
endmodule

module Not (
  input  [3:0] in_1,
  output [3:0] out_2
);

  not not_1 (out_2[0], in_1[0]);
  not not_2 (out_2[1], in_1[1]);
  not not_3 (out_2[2], in_1[2]);
  not not_4 (out_2[3], in_1[3]);
endmodule

module And (
  input  [3:0] A,
  input  [3:0] B,
  output [3:0] out_3
);

  and and_1 (out_3[0], A[0], B[0]);
  and and_2 (out_3[1], A[1], B[1]);
  and and_3 (out_3[2], A[2], B[2]);
  and and_4 (out_3[3], A[3], B[3]);
endmodule

module A (
  input  a,
  input  b,
  input  c,
  input  d,
  output x
);

  wire and_1_out, and_2_out, and_3_out, and_4_out, and_5_out, and_6_out, not_1_out, not_2_out, not_3_out,
       not_4_out, not_5_out, not_6_out, not_7_out, not_8_out, not_9_out;

  not not_1 (not_1_out, a);
  not not_2 (not_2_out, b);
  not not_3 (not_3_out, d);
  not not_4 (not_4_out, b);
  not not_5 (not_5_out, a);
  not not_6 (not_6_out, b);
  not not_7 (not_7_out, c);
  not not_8 (not_8_out, c);
  not not_9 (not_9_out, d);
  and and_1 (and_1_out, not_1_out, not_2_out, not_3_out);
  and and_2 (and_2_out, not_4_out, c, d);
  and and_3 (and_3_out, not_5_out, b, d);
  and and_4 (and_4_out, a, not_6_out, not_7_out);
  and and_5 (and_5_out, a, not_8_out, d);
  and and_6 (and_6_out, a, b, c, not_9_out);
  or or_1 (x, and_1_out, and_2_out, and_3_out, and_4_out, and_5_out, and_6_out);
endmodule

module B (
  input  a,
  input  b,
  input  c,
  input  d,
  output x
);

  wire and_1_out, and_2_out, and_3_out, and_4_out, and_5_out, not_1_out, not_2_out, not_3_out, not_4_out,
       not_5_out, not_6_out, not_7_out;

  not not_1 (not_1_out, a);
  and and_1 (and_1_out, not_1_out, not_2_out);
  not not_2 (not_2_out, b);
  not not_3 (not_3_out, b);
  and and_2 (and_2_out, not_3_out, not_4_out);
  not not_4 (not_4_out, c);
  not not_5 (not_5_out, c);
  and and_3 (and_3_out, not_5_out, not_6_out);
  not not_6 (not_6_out, d);
  not not_7 (not_7_out, a);
  and and_4 (and_4_out, not_7_out, c, d);
  and and_5 (and_5_out, a, b);
  or or_1 (x, and_1_out, and_2_out, and_3_out, and_4_out, and_5_out);
endmodule

module C (
  input  a,
  input  b,
  input  c,
  input  d,
  output x
);

  wire and_1_out, and_2_out, not_1_out, not_2_out, not_3_out;

  not not_1 (not_1_out, c);
  not not_2 (not_2_out, a);
  and and_1 (and_1_out, not_2_out, b);
  and and_2 (and_2_out, a, not_3_out);
  not not_3 (not_3_out, b);
  or or_1 (x, not_1_out, d, and_1_out, and_2_out);
endmodule

module D (
  input  a,
  input  b,
  input  c,
  input  d,
  output x
);

  wire and_1_out, and_2_out, and_3_out, and_4_out, not_1_out, not_2_out, not_3_out, not_4_out, not_5_out;

  not not_1 (not_1_out, b);
  and and_1 (and_1_out, not_1_out, not_2_out);
  not not_2 (not_2_out, d);
  not not_3 (not_3_out, b);
  and and_2 (and_2_out, not_3_out, c);
  and and_3 (and_3_out, c, not_4_out);
  not not_4 (not_4_out, d);
  not not_5 (not_5_out, c);
  and and_4 (and_4_out, b, not_5_out, d);
  or or_1 (x, and_1_out, and_2_out, and_3_out, and_4_out);
endmodule

module E (
  input  a,
  input  b,
  input  c,
  input  d,
  output x
);

  wire and_1_out, and_2_out, not_1_out, not_2_out, not_3_out;

  not not_1 (not_1_out, b);
  and and_1 (and_1_out, not_1_out, not_2_out);
  not not_2 (not_2_out, d);
  and and_2 (and_2_out, c, not_3_out);
  not not_3 (not_3_out, d);
  or or_1 (x, and_1_out, and_2_out);
endmodule

module F (
  input  a,
  input  b,
  input  c,
  input  d,
  output x
);

  wire and_1_out, and_2_out, and_3_out, and_4_out, not_1_out, not_2_out, not_3_out, not_4_out, not_5_out,
       not_6_out, not_7_out;

  not not_1 (not_1_out, c);
  and and_1 (and_1_out, not_1_out, not_2_out);
  not not_2 (not_2_out, d);
  not not_3 (not_3_out, a);
  and and_2 (and_2_out, not_3_out, b, not_4_out);
  not not_4 (not_4_out, c);
  not not_5 (not_5_out, a);
  and and_3 (and_3_out, not_5_out, b, not_6_out);
  not not_6 (not_6_out, d);
  not not_7 (not_7_out, b);
  and and_4 (and_4_out, a, not_7_out, c);
  or or_1 (x, and_1_out, and_2_out, and_3_out, and_4_out);
endmodule

module G (
  input  a,
  input  b,
  input  c,
  input  d,
  output x
);

  wire and_1_out, and_2_out, and_3_out, and_4_out, not_1_out, not_2_out, not_3_out, not_4_out;

  not not_1 (not_1_out, b);
  and and_1 (and_1_out, not_1_out, c);
  and and_2 (and_2_out, b, not_2_out);
  not not_2 (not_2_out, c);
  and and_3 (and_3_out, b, not_3_out);
  not not_3 (not_3_out, d);
  and and_4 (and_4_out, a, not_4_out);
  not not_4 (not_4_out, d);
  or or_1 (x, and_1_out, and_2_out, and_3_out, and_4_out);
endmodule

module H (
  input  a,
  input  b,
  input  c,
  input  d,
  output x
);


  assign x = a;
endmodule

module Displays (
  input  in_1,
  input  in_2,
  input  in_3,
  input  in_4,
  output A,
  output B,
  output C,
  output D,
  output E,
  output F,
  output G,
  output H
);

  A a_1 (.a(in_1), .b(in_2), .c(in_3), .d(in_4), .x(A));
  B b_1 (.a(in_1), .b(in_2), .c(in_3), .d(in_4), .x(B));
  C c_1 (.a(in_1), .b(in_2), .c(in_3), .d(in_4), .x(C));
  D d_1 (.a(in_1), .b(in_2), .c(in_3), .d(in_4), .x(D));
  E e_1 (.a(in_1), .x(E), .b(in_2), .c(in_3), .d(in_4));
  F f_1 (.a(in_1), .b(in_2), .c(in_3), .d(in_4), .x(F));
  G g_1 (.a(in_1), .b(in_2), .c(in_3), .d(in_4), .x(G));
  H h_1 (.a(in_1), .b(in_2), .c(in_3), .d(in_4), .x(H));
endmodule
